# Fritzing sketch macchina_raggi_x (saved by Fritzing 0.9.10b)
breadboards: 2

parts:
  Mod1 = Heltec WiFi LoRa 32 V2 [part_number=HTIT-WB32LA]
  C1 = Capacitor [package=cap-pth-small2]
  WeMos_D1_Mini_Relay_Shield_V1 = WeMos D1 Mini Relay Shield V2
  WeMos_D1_Mini_Relay_Shield_V2 = WeMos D1 Mini Relay Shield V2
  Q1 = TRANSISTOR_NPN [package=to-92]
  Q2 = TRANSISTOR_NPN [package=to-92]
  R1 = Resistor [tolerance=±5% resistance=100k package="0402 [SMD]"]
  R2 = Resistor [tolerance=±5% resistance=100k package="0402 [SMD]"]
  D1 = Diode [package=diode-1n4148]
  D2 = Diode [package=diode-1n4148]
  C2 = Capacitor [package=cap-pth-small2]
  C3 = Capacitor [package=cap-pth-small2]
  D3 = Diode [package=diode-1n4148]
  D4 = Diode [package=diode-1n4148]
  C4 = Capacitor [package=cap-pth-small2]
  U1 = Transformer [package=transformer]
  C5 = Film/Foil Capacitor [capacitance=100nF voltage=35V package="15mm [THT, pp]"]
  D6 = Zener Diode [part_number=1N4732A breakdown_voltage=3.6V package="300 mil [THT]"]
  D8 = Diode [package=diode-1n4148]
  Q5 = npn-Powertransistor [package="TO220 [THT]"]
  Q6 = npn-Powertransistor [package="TO220 [THT]"]
  R5 = Resistor [tolerance=±5% resistance=10k package="0402 [SMD]"]
  D9 = Zener Diode [part_number=1N4732A breakdown_voltage=3.6V package="300 mil [THT]"]
  R8 = Resistor [tolerance=±5% resistance=10k package="0402 [SMD]"]
  R9 = Resistor [tolerance=±5% resistance=470 power=3W package="0402 [SMD]"]
  R10 = Resistor [tolerance=±5% resistance=470 power=3W package="0402 [SMD]"]
  L1 = Inductor [inductance=200µH package="400 mil [THT]"]
  D10 = Diode [package=diode-1n4148]
  U2 = Transformer [package=transformer]
  U3 = Transformer [package=transformer]
  D11 = Diode [package=diode-1n4148]
  D12 = Diode [package=diode-1n4148]
  D13 = Diode [package=diode-1n4148]
  D14 = Diode [package=diode-1n4148]
  C6 = Ceramic Capacitor [capacitance="100 nF" voltage=35V package="0603 [SMD, multilayer]"]
  F1 = FUSE [package=fuse_5mm]
  AM1 = Multimeter (AC Current)
  R11 = Resistor [tolerance=±5% resistance=220 package="0402 [SMD]"]

nets:
  N1: Mod1.pin_16, Mod1.pin_17
  N2: Mod1.GND, WeMos_D1_Mini_Relay_Shield_V1.G, WeMos_D1_Mini_Relay_Shield_V2.G, Q2.C
  5V: Mod1.pin_20, WeMos_D1_Mini_Relay_Shield_V1.5V, WeMos_D1_Mini_Relay_Shield_V2.5V, Q1.C
  N3: Mod1.pin_21, Mod1.pin_22
  N4: Mod1.pin_35, R2.Pin_1
  N5: Mod1.pin_36, R1.Pin_1
  N6: C1.1, U1.4
  N7: C1.2, D1.C, D2.A, C3.1
  N8: WeMos_D1_Mini_Relay_Shield_V1.D0, Q2.E
  N9: WeMos_D1_Mini_Relay_Shield_V2.D0, Q1.E
  N10: Q1.B, R2.Pin_0
  N11: Q2.B, R1.Pin_0
  N12: D1.A, C2.2, U1.3
  N13: D2.C, C2.1, D4.A, C4.2
  N14: C3.2, D3.A, D4.C
  N15: D3.C, C4.1
  N16: U1.1, C5.-, D8.C, Q5.collector
  N17: U1.2, C5.+, Q6.collector, D10.C
  N18: D6.cathode, D6.anode, Q5.base, Q5.emitter, Q6.emitter, R5.Pin_0, R5.Pin_1, D9.anode, R8.Pin_0, R9.Pin_1, D10.A, D11.A, D13.A, C6.1
  N19: D8.A, Q6.base, D9.cathode, R10.Pin_1
  N20: R9.Pin_0, R10.Pin_0, L1.pin_0, D12.C, D14.C, C6.0
  N21: U2.3, R11.Pin_0
  N22: U2.4, AM1.A_Probe
  N23: U3.3, D13.C, D14.A
  N24: U3.4, D11.C, D12.A
  N25: F1.1, AM1.COM_Probe
  N26: F1.2, R11.Pin_1

notes:
  Alimentazione 220V 50Hz AC
  TUBO RAGGI X
  Trasformatore flyback
  Moltiplicatore di tensione
  ZVS driver
  Alimentatore 24V DC
  Alimentatore per filamento
